// Logisim project logic.circ as structural Verilog: 4 circuits, main circuit main
module main (
);

  D_Flip_Flop d_ff_1 ();  // open: clk, D, Q, Qn, preset, en, reset
endmodule

module Full_Adder (
  input  A,
  input  B,
  input  Cin,
  output S,
  output Cout
);

  wire and_1_out, and_2_out, xor_1_out;

  xor xor_1 (xor_1_out, A, B);
  xor xor_2 (S, xor_1_out, Cin);
  and and_1 (and_1_out, xor_1_out, Cin);
  and and_2 (and_2_out, A, B);
  or or_1 (Cout, and_1_out, and_2_out);
endmodule

module _8_bit_Adder (
  input  A1,
  input  B1,
  input  A2,
  input  B2,
  input  A3,
  input  B3,
  input  A4,
  input  B4,
  input  A5,
  input  B5,
  input  A6,
  input  B6,
  input  A7,
  input  B7,
  input  A8,
  input  B8,
  output out_17,
  output out_18,
  output out_19,
  output out_20,
  output out_21,
  output out_22,
  output out_23,
  output out_24,
  output Overflow
);

  wire full_adder_1_cout, full_adder_2_cout, full_adder_3_cout, full_adder_4_cout, full_adder_5_cout,
       full_adder_6_cout, full_adder_7_cout;

  Full_Adder full_adder_1 (.A(A1), .B(B1), .Cin(1'b0), .S(out_17), .Cout(full_adder_1_cout));
  Full_Adder full_adder_2 (.A(A2), .B(B2), .Cin(full_adder_1_cout), .S(out_18), .Cout(full_adder_2_cout));
  Full_Adder full_adder_3 (.A(A3), .B(B3), .Cin(full_adder_2_cout), .S(out_19), .Cout(full_adder_3_cout));
  Full_Adder full_adder_4 (.A(A4), .B(B4), .Cin(full_adder_3_cout), .S(out_20), .Cout(full_adder_4_cout));
  Full_Adder full_adder_5 (.A(A5), .B(B5), .Cin(full_adder_4_cout), .S(out_21), .Cout(full_adder_5_cout));
  Full_Adder full_adder_6 (.A(A6), .B(B6), .Cin(full_adder_5_cout), .S(out_22), .Cout(full_adder_6_cout));
  Full_Adder full_adder_7 (.A(A7), .B(B7), .Cin(full_adder_6_cout), .S(out_23), .Cout(full_adder_7_cout));
  Full_Adder full_adder_8 (.A(A8), .B(B8), .Cin(full_adder_7_cout), .S(out_24), .Cout(Overflow));
endmodule

module IncrementationDecrementationUnit (
  input  INCREMENT,
  input  DECREMENT,
  input  IN1,
  input  IN2,
  input  IN3,
  input  IN4,
  input  IN5,
  input  IN6,
  input  IN7,
  input  IN8,
  output O1,
  output O2,
  output O3,
  output O4,
  output O5,
  output O6,
  output O7,
  output O8,
  output Overflow
);

  wire and_1_out, and_2_out, or_1_out;

  and and_1 (and_1_out, INCREMENT, 1'b1);
  and and_2 (and_2_out, DECREMENT, 1'b1);
  or or_1 (or_1_out, and_1_out, and_2_out);
  _8_bit_Adder u_8_bit_adder_1 (
    .A1(IN1), .B1(or_1_out), .A2(IN2), .B2(and_2_out), .A3(IN3), .B3(and_2_out), .A4(IN4), .B4(and_2_out),
    .A5(IN5), .B5(and_2_out), .A6(IN6), .B6(and_2_out), .A7(IN7), .B7(and_2_out), .A8(IN8), .B8(and_2_out),
    .out_17(O1), .out_18(O2), .out_19(O3), .out_20(O4), .out_21(O5), .out_22(O6), .out_23(O7), .out_24(O8),
    .Overflow(Overflow));
endmodule
